# Fritzing sketch Eksamen (saved by Fritzing 0.9.3b)
breadboards: 1

parts:
  Part1 = Photon
  R1 = Resistor [tolerance=±5% resistance=1k package="2010 [SMD]"]
  R2 = Resistor [tolerance=±5% resistance=1k package="2010 [SMD]"]
  R3 = Resistor [tolerance=±5% resistance=1k package="2010 [SMD]"]
  R4 = Resistor [tolerance=±5% resistance=1k package="2010 [SMD]"]
  R5 = Resistor [tolerance=±5% resistance=1k package="2010 [SMD]"]
  S1 = Pushbutton [package="[THT]"]
  S2 = Pushbutton [package="[THT]"]
  S3 = Pushbutton [package="[THT]"]

nets:
  N1: Part1.GND, R1.Pin_0, R2.Pin_0, R3.Pin_0
  N2: Part1.VIN, R4.Pin_0, R5.Pin_0, S1.Pin_1, S1.Pin_2, S2.Pin_1, S2.Pin_2, S3.Pin_1, S3.Pin_2
  N3: Part1.D0, R4.Pin_1
  N4: Part1.D1, R5.Pin_1
  N5: Part1.D5, R3.Pin_1, S2.Pin_3, S2.Pin_4
  N6: Part1.D6, R1.Pin_1, S1.Pin_3, S1.Pin_4
  N7: Part1.D7, R2.Pin_1, S3.Pin_3, S3.Pin_4
